# Fritzing sketch watchduino2-atmega328 (saved by Fritzing 0.9.2b)
circuit board: 2.5cm x 2.5cm

parts:
  OLED1 = 128x64 Monochrom OLED Display with I2C Control
  Parte1 = Bluetooth HC-05 Macho  # not connected
  U1 = LIPO-110mAh [package=lipo-110]  # not connected
  MOTOR1 = Vibration Motor
  U2 = ATmega328 [package=tqfp]
  Y1 = CRYSTAL [package=crystal-smd-5x3]
  JP1 = Header 2 [package=jst-2-pth]
  JP3 = Header 4 [package=molex-1x4_lock]
  JP4 = Header 6 [package=molex-1x6_lock]
  Left = Header 2 [package=screwterminal-3.5mm-2_lock]
  Select = Header 2 [package=screwterminal-3.5mm-2_lock]
  Right = Header 2 [package=screwterminal-3.5mm-2_lock]
  Menu = Header 2 [package=screwterminal-3.5mm-2_lock]
  JP5 = Header 4 [package=molex-1x4_lock]

nets (from the pcb view):
  N1: OLED1.SCL, OLED1.SCA
  N2: MOTOR1.POS, U2.PD6(AIN0)
  N3: MOTOR1.NEG, U2.AGND, JP1.1, Left.1, Menu.2, JP5.1
  N4: U2.PD4(XCK_T0), Select.1
  N5: U2.GND, Select.2, Right.1
  N6: U2.VCC, JP1.2, JP3.1, JP4.4, JP5.2
  N7: U2.PB6(XTAL1_TOSC1), Y1.1
  N8: U2.PB7(XTAL2_TOSC2), Y1.2
  N9: U2.PD5(T1), Left.2
  N10: U2.PB1(OC1A), JP5.3
  N11: U2.PB2(SS_OC1B), JP5.4
  N12: U2.PB3(MOSI_OC2), Right.2
  N13: U2.PC4(ADC4_SDA), JP3.4
  N14: U2.PC5(ADC5_SCL), JP3.3
  N15: U2.PC6(_RESET), JP4.2
  N16: U2.PD0(RXD), JP3.2, JP4.3, JP4.6
  N17: U2.PD1(TXD), JP4.5
  N18: U2.PD2(INT0), Menu.1

custom parts:
  Vibration Motor: An eccentric vibration motor!
