# Fritzing sketch watchduino2 (saved by Fritzing 0.9.1b)

parts:
  OLED1 = 128x64 Monochrom OLED Display with I2C Control
  Parte1 = Bluetooth HC-05 Macho
  Right = Pushbutton [package=THT]
  Left = Pushbutton [package=THT]
  Menu = Pushbutton [package=THT]
  J1 = Piezo Speaker
  U1 = LIPO-110mAh [package=lipo-110]
  Q1 = NPN-Transistor [package="TO92 [THT]"]
  Parte2 = Arduino Pro Mini v13
  Select = Pushbutton [package=THT]
  MOTOR1 = Vibration Motor

nets:
  N1: OLED1.SCL, Parte2.A4
  N2: OLED1.SCA, Parte2.A5
  VCC: OLED1.VCC, U1.+, Q1.B, Parte2.VCC
  GND: OLED1.GND, Parte1.GND, Right.leg1, Left.leg0, Menu.leg0, J1.pin1, U1.-, Parte2.GND, Select.leg1, MOTOR1.NEG
  N3: Parte1.TXD, Parte2.D9_PWM
  N4: Parte1.RXD, Parte2.D10_PWM/SS
  N5: Parte1.VCC, Q1.E
  N6: Right.leg0, Parte2.D4
  N7: Left.leg1, Parte2.D5_PWM
  N8: Menu.leg1, Parte2.D2
  N9: J1.pin2, Parte2.D12/MISO
  N10: Q1.C, Parte2.D8
  N11: Parte2.D11_PWM/MOSI, MOTOR1.POS
  N12: Parte2.D6_PWM, Select.leg0

custom parts:
  Vibration Motor: An eccentric vibration motor!
